# Fritzing sketch Sensor_PCB_V0_2 (saved by Fritzing 0.9.10b)
circuit board: 11.712cm x 6.95454cm
breadboards: 1

parts:
  Gyro = female pin header, 8 pins [form="♀ (female)"]
  Arduino = Arduino Mega ADK (Rev3)
  WiFi = shrouded pin header, 8 pins [form="♂ (shrouded male)"]
  GSM = female pin header, 6 pins [form="♀ (female)"]
  ANT = Antenna
  ANT_2 = SMA Antenna Connector RA 6mm pad spacing
  GPS = female pin header, 4 pins [form="♀ (female)"]
  Temp_Sen = female pin header, 3 pins [form="♀ (female)"]
  R2 = Resistor [tolerance=±5% resistance=4.7 power=0.25 package=THT]
  oled = female pin header, 4 pins [form="♀ (female)"]
  Turbidity_Sen = female pin header, 3 pins [form="♀ (female)"]
  Solar_Charge = double row female pin header, 2 pins [form="♀ (female)"]

nets:
  N1: Gyro.pin1, Arduino.IOREF, Arduino.5V, GSM.pin2, GPS.pin1, Temp_Sen.pin1, R2.Pin_0, oled.pin3, Turbidity_Sen.pin3
  N2: Gyro.pin2, Arduino.GND, WiFi.pin4, GSM.pin6, GPS.pin4, Temp_Sen.pin2, oled.pin4, Turbidity_Sen.pin1, Solar_Charge.pin2
  N3: Gyro.pin3, Arduino.D21/SCL, oled.pin2
  N4: Gyro.pin4, Arduino.D20/SDA, oled.pin1
  N5: Arduino.A0, Turbidity_Sen.pin2
  N6: Arduino.D19/RX1, GSM.pin4
  N7: Arduino.D18/TX1, GSM.pin5
  N8: Arduino.D17/RX2, GPS.pin3
  N9: Arduino.D16/TX2, GPS.pin2
  N10: Arduino.3V3, WiFi.pin6, WiFi.pin7, WiFi.pin8
  N11: Arduino.VIN, Solar_Charge.pin1
  N12: Arduino.D0/RX0, WiFi.pin1
  N13: Arduino.D1/TX0, WiFi.pin5
  N14: Arduino.D38, Temp_Sen.pin3, R2.Pin_1
  N15: GSM.pin1, ANT.antenna_lead, ANT_2.SIGNAL

notes:
  MANUFACTURED WITH LOVE FROM INDIA
  DESIGNED BY THEACCELOGUY
  OCEAN SENSOR MONITORING BOARD V0.2
  FABFEST BALI 2022

custom parts:
  SMA Antenna Connector RA 6mm pad spacing: SMA RA Antenna Connector with 6mm pcb pad spacing.
